# Fritzing sketch coop_controller (saved by Fritzing 0.9.2b)
breadboards: 1

parts:
  Part1 = Arduino Uno (Rev3)
  Power_plug1 = Power plug [part_number="12v power supply"]
  M1 = DC Motor [part_number="12v 30 RPM"]
  U1 = L298_BRIDGE_DRIVER [package=powerso20]
  R1 = Photocell (LDR) [package=THT]
  R2 = Resistor [tolerance=±5% resistance=10k package=THT]
  S3 = SWITCH-SP3T [package=switch-sp3t-smd]
  S4 = Reed switch [part_number="Top Switch" package=THT]
  S5 = Reed switch [part_number="Bottom Switch" package=THT]
  LED1 = LED - 5mm [color="Red (633nm)" package="5 mm [THT]"]
  R3 = Resistor [tolerance=±5% resistance=10k package=THT]

nets:
  N1: Part1.A0, R1.pin_1
  N2: Part1.D8, U1.IN2
  N3: Part1.D9_PWM, LED1.anode
  GND: Part1.GND, Power_plug1.GND, U1.GND, R2.Pin_1
  N4: Part1.D2, S3.4
  N5: Part1.D3_PWM, S3.2
  N6: Part1.D4, S5.pin_1
  N7: Part1.D5_PWM, S4.pin_1
  N8: Part1.D6_PWM, U1.ENA
  N9: Part1.D7, U1.IN1
  5V: Part1.5V, S3.3, S4.pin_2, S5.pin_2
  VIN: Part1.VIN, Power_plug1.VCC, U1.VS
  N10: M1.pin_1, U1.OUT2
  N11: M1.pin_2, U1.OUT1
  N12: R1.pin_0, R2.Pin_0
  N13: LED1.cathode, R3.Pin_0
